# Fritzing sketch RobotArmfzz (saved by Fritzing 0.9.2b)
breadboards: 1

parts:
  D1 = Rectifier Diode [part_number=1N4001 package="300 mil [THT]"]
  S1 = Pushbutton [package="[THT]"]
  U1 = atmega328 [package=dip]
  J1 = Basic Servo
  R1 = Rotary Potentiometer (Large) [maximum_resistance=100kΩ package=THT]
  J2 = Power Jack [package=power_jack_pth]
  S2 = Pushbutton [package="[THT]"]
  S3 = Pushbutton [package="[THT]"]
  R2 = Resistor [tolerance=±5% resistance=220 package=THT]
  R3 = Resistor [tolerance=±5% resistance=220 package=THT]
  R4 = Resistor [tolerance=±5% resistance=220 package=THT]
  IC1 = Voltage Regulator [package=to-220-alt]
  J3 = Basic Servo
  J4 = Basic Servo
  J5 = Basic Servo
  R5 = Rotary Potentiometer (Large) [maximum_resistance=100kΩ package=THT]
  R6 = Rotary Potentiometer (Large) [maximum_resistance=100kΩ package=THT]
  R7 = Rotary Potentiometer (Large) [maximum_resistance=100kΩ package=THT]
  C1 = Electrolytic Capacitor [capacitance=1µF package="100 mil [THT, electrolytic]"]
  C2 = Electrolytic Capacitor [capacitance=1µF package="100 mil [THT, electrolytic]"]
  U2 = SN74LS14N [package="DIP14 [THT]"]
  C3 = Electrolytic Capacitor [capacitance=1µF package="100 mil [THT, electrolytic]"]
  C4 = Electrolytic Capacitor [capacitance=1µF package="100 mil [THT, electrolytic]"]
  C5 = Electrolytic Capacitor [capacitance=1µF package="100 mil [THT, electrolytic]"]
  C6 = Electrolytic Capacitor [capacitance=1µF package="100 mil [THT, electrolytic]"]
  D2 = Rectifier Diode [part_number=1N4001 package="300 mil [THT]"]
  C7 = Electrolytic Capacitor [capacitance=1µF package="100 mil [THT, electrolytic]"]
  D3 = Rectifier Diode [part_number=1N4001 package="300 mil [THT]"]
  C8 = Electrolytic Capacitor [capacitance=1µF package="100 mil [THT, electrolytic]"]
  D4 = Rectifier Diode [part_number=1N4001 package="300 mil [THT]"]
  C9 = Electrolytic Capacitor [capacitance=1µF package="100 mil [THT, electrolytic]"]
  C10 = Electrolytic Capacitor [capacitance=1µF package="100 mil [THT, electrolytic]"]
  C11 = Electrolytic Capacitor [capacitance=1µF package="100 mil [THT, electrolytic]"]
  C12 = Electrolytic Capacitor [capacitance=1µF package="100 mil [THT, electrolytic]"]
  C13 = Electrolytic Capacitor [capacitance=1µF package="100 mil [THT, electrolytic]"]

nets:
  N1: D1.cathode, IC1.IN, C1.+
  N2: D1.anode, J2.PWR
  N3: S1.Pin_1, S1.Pin_2, R3.Pin_0, D2.anode
  GND: S1.Pin_3, S1.Pin_4, U1.GND#7, J2.GND, J2.GNDBREAK, S2.Pin_3, S2.Pin_4, S3.Pin_3, S3.Pin_4, IC1.GND, C2.-, U2.GND, C7.-, C8.-, C9.-
  N4: U1.D2, U2.1Y
  N5: U1.D3_(PWM), J1.pulse
  VCC: U1.VCC, J1.vcc, R1.leg2, IC1.OUT, R5.leg2, R6.leg2, R7.leg2, C2.+, U2.VCC, C10.+, C11.+, C12.+, C13.+
  N6: U1.D9_(PWM), J3.pulse
  N7: U1.D10_(PWM), J4.pulse
  N8: U1.D11_(PWM), J5.pulse
  N9: U1.D12, U2.2Y
  N10: U1.D13, U2.3Y
  GND_2: U1.GND#21, J1.gnd, R1.leg1, J3.gnd, J4.gnd, J5.gnd, R5.leg1, R6.leg1, R7.leg1, C3.-, C4.-, C5.-, C6.-, C10.-, C11.-, C12.-, C13.-
  N11: U1.A0, R7.wiper
  N12: U1.A1, R5.wiper
  N13: U1.A2, R6.wiper
  N14: U1.A3, R1.wiper
  N15: S2.Pin_1, S2.Pin_2, S3.Pin_1, S3.Pin_2, R2.Pin_0, R4.Pin_0, D3.anode, D4.anode
  N16: R2.Pin_1, U2.2A, D3.cathode, C8.+
  N17: R3.Pin_1, U2.1A, D2.cathode, C7.+
  N18: R4.Pin_1, U2.3A, D4.cathode, C9.+
  VCC_2: J3.vcc, J4.vcc, J5.vcc, C3.+, C4.+, C5.+, C6.+
